# Fritzing sketch CampStone (saved by Fritzing 0.9.4)
breadboards: 1

parts:
  Argon1 = Particle Argon
  Mod1 = KY-026 Flame Sensor Module [package="Breakout board"]
  OLED_I2C1 = OLED 128x64 I2C Monochrome Display
  M1 = BMP280
  Part1 = Ambient Light Sensor (TEMT6000 Breakout Board)
  LED1 = smd LED [color="Green (570nm)" package="0805 [SMD]"]
  LED2 = smd LED [color="Red (633nm)" package="1206 [SMD]"]
  R1 = Resistor [tolerance=±5% resistance=220 package=THT]
  R2 = Resistor [tolerance=±5% resistance=220 package=THT]
  U1 = AQ_Sensor [package=mq-3]
  Neopixel1 = Adafruit RBG Smart Neopixel [package="DIP (Dual Inline) [THT]"]

nets:
  VCC: Argon1.3.3V, Mod1.+, OLED_I2C1.VDD, M1.VIN, Part1.VCC, U1.Vcc
  GND: Argon1.GND, Mod1.G, OLED_I2C1.GND, M1.GND, Part1.GND, R1.Pin_1, R2.Pin_1, U1.GND, Neopixel1.G
  N1: Argon1.A1, Mod1.A0
  N2: Argon1.A3, Part1.S
  N3: Argon1.SDA, OLED_I2C1.SDA, M1.SDA
  N4: Argon1.SCL, OLED_I2C1.SCK, M1.SCL
  N5: Argon1.D4, LED2.anode
  N6: Argon1.D5, LED1.anode
  N7: Argon1.D7, Neopixel1.+
  N8: Argon1.VUSB, Neopixel1.In
  N9: LED1.cathode, R2.Pin_0
  N10: LED2.cathode, R1.Pin_0

custom parts:
  Particle Argon: The Argon is a powerful Wi-Fi enabled development board that can act as either a standalone Wi-Fi endpoint or Wi-Fi enabled gateway for Particle Mesh networks. It is based on the Nordic nRF52840 and has built-in battery charging circuitry so it’s easy to connect a Li-Po and deploy your local network in minutes. The Argon is great for connecting existing projects to the Particle Device Cloud or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
  KY-026 Flame Sensor Module: KY-026 Flame Sensor Module reacts in the presence of fire.
  BMP280: Temperature Humidity Barometric presure Sensor, I2C
  AQ_Sensor: MQ-3 alcohol gas sensor . FP not tested. SEN-08880.
